# Fritzing sketch time_recorder (saved by Fritzing 0.9.3b)
breadboards: 1

parts:
  パーツ1 = Arduino Uno (Rev3)
  Parallax_RFID_Reader_Module2 = Parallax RFID Reader Module
  LED1 = LED - 5mm [color="Red (633nm)" package="5 mm [THT]"]
  LED2 = LED - 5mm [color="Infrared (940nm)" package="5 mm [THT]"]
  S4 = Momentary Switch [package=ksa_sealed_tac_switch]
  S5 = Momentary Switch [package=ksa_sealed_tac_switch]
  R4 = Resistor [tolerance=±5% resistance=510 package=THT]
  R5 = Resistor [tolerance=±5% resistance=510 package=THT]

nets:
  N1: パーツ1.D8, Parallax_RFID_Reader_Module2./ENABLE
  N2: パーツ1.D9_PWM, Parallax_RFID_Reader_Module2.Sout
  N3: パーツ1.D10_PWM/SS, LED2.anode
  N4: パーツ1.D11_PWM/MOSI, LED1.anode
  N5: パーツ1.D12/MISO, S5.2, R4.Pin_1
  N6: パーツ1.D13/SCK, S4.2, R5.Pin_1
  5V: パーツ1.5V, Parallax_RFID_Reader_Module2.VCC, S4.4, S5.4
  GND: パーツ1.GND, Parallax_RFID_Reader_Module2.GND, LED1.cathode, LED2.cathode, R4.Pin_0, R5.Pin_0
